# Fritzing sketch Sketch (saved by Fritzing 0.9.3b)
breadboards: 1

parts:
  Part1 = songle relay
  Part2 = Arduino Nano (Rev3.0)
  R1 = Resistor [tolerance=±5% resistance=220 package="0402 [SMD]"]  # not connected
  R2 = Resistor [tolerance=±5% resistance=1k package="0402 [SMD]"]
  LED1 = smd LED [color="Red (633nm)" package="0805 [SMD]"]
  D1 = Diode [package=diode-1n4001]
  Q1 = NPN-Transistor [package="TO92 [THT]"]  # not connected

nets:
  N1: Part1.NO, LED1.anode
  N2: Part1.GND, D1.A
  N3: Part2.D2, R2.Pin_0
